# Fritzing sketch self (saved by Fritzing 0.8.7b)
breadboards: 1

parts:
  Part1 = Arduino Uno (Rev3)
  GY1 = MPU-6050 Board GY-521 [form="♀ (female)" package=THT]
  LED1 = LED - 5mm [color="Red (633nm)" package="5 mm [THT]"]
  S1 = Pushbutton [package="[THT]"]
  R1 = Resistor [tolerance=±5% resistance=10k package=THT]
  IC1 = L293D [package=THT]
  VCC1 = 4 x AAA Battery Mount
  M1 = DC Motor
  M2 = DC Motor
  Part2 = Bluetooth HC-05 Macho

nets:
  N1: Part1.A4/SDA, GY1.pin3
  N2: Part1.A5/SCL, GY1.pin4
  N3: Part1.D8, IC1.In_1
  N4: Part1.D9_PWM, IC1.In_2
  N5: Part1.D10_PWM/SS, IC1.In_4
  N6: Part1.D11_PWM/MOSI, IC1.In_3
  N7: Part1.D0/RX, Part2.TXD
  N8: Part1.D1/TX, Part2.RXD
  N9: Part1.D2, LED1.anode, S1.Pin_3, S1.Pin_4
  N10: Part1.D3_PWM, IC1.Enable_2
  N11: Part1.D5_PWM, IC1.Enable_1
  5V: Part1.5V, GY1.pin1, R1.Pin_1, Part2.VCC
  GND: Part1.GND, GY1.pin2, LED1.cathode, IC1.0V, IC1.+V, VCC1.+, Part2.GND
  N12: S1.Pin_1, S1.Pin_2, R1.Pin_0
  N13: IC1.Out_1_(_Controlled_by_Enable_1_), M1.pin_2
  N14: IC1.Out_2_(_Controlled_by_Enable_1_), M1.pin_1
  N15: IC1.+Vmotor, VCC1.-
  N16: IC1.Out_3_(_Controlled_by_Enable_2_), M2.pin_2
  N17: IC1.Out_4_(_Controlled_by_Enable_2_), M2.pin_1

custom parts:
  MPU-6050 Board GY-521: Acelerometro y Giroscopio MPU-6050 Board GY-521
